// Logisim project 231_ASSIGNMENT.circ as structural Verilog: 1 circuit, main circuit main
module main (
  output Q3,
  output Q2,
  output Q1,
  output Q0
);

  wire and_1_out, and_2_out, and_3_out, and_4_out, and_5_out, and_6_out, and_7_out, and_8_out, and_9_out,
       and_10_out, and_11_out, and_12_out, and_13_out, clock_1_out, FF0_qn, FF1_qn, FF2_qn, FF3_qn, or_1_out,
       or_2_out, or_3_out, or_4_out, or_5_out, or_6_out, or_7_out, or_8_out;

  or or_1 (or_1_out, and_1_out, and_2_out, and_3_out);
  or or_2 (or_2_out, and_2_out, and_6_out);
  Clock clock_1 (.out(clock_1_out));
  and and_1 (and_1_out, Q0, Q1, Q2, Q3);
  and and_2 (and_2_out, FF3_qn, FF2_qn, Q3);
  and and_3 (and_3_out, Q0, FF2_qn, FF0_qn);
  J_K_Flip_Flop FF0 (.J(or_3_out), .clk(clock_1_out), .K(or_1_out), .Q(Q3), .Qn(FF0_qn));  // open: preset, en, reset
  and and_4 (and_4_out, FF0_qn, FF1_qn, FF2_qn);
  or or_3 (or_3_out, and_4_out, and_5_out);
  and and_5 (and_5_out, FF0_qn, FF1_qn, FF3_qn);
  and and_6 (and_6_out, Q3, Q2, Q0);
  and and_7 (and_7_out, FF0_qn, FF1_qn);
  or or_4 (or_4_out, and_7_out, and_11_out);
  or or_5 (or_5_out, and_8_out, and_5_out);
  J_K_Flip_Flop FF1 (.J(or_5_out), .clk(clock_1_out), .K(or_2_out), .Q(Q2), .Qn(FF1_qn));  // open: preset, en, reset
  and and_8 (and_8_out, FF2_qn, Q0);
  J_K_Flip_Flop FF2 (.J(or_6_out), .clk(clock_1_out), .K(or_4_out), .Q(Q1), .Qn(FF2_qn));  // open: preset, en, reset
  and and_9 (and_9_out, FF3_qn, Q1, FF0_qn);
  and and_10 (and_10_out, Q3, Q2);
  and and_11 (and_11_out, Q3, FF2_qn);
  J_K_Flip_Flop FF3 (.J(or_7_out), .clk(clock_1_out), .K(or_8_out), .Q(Q0), .Qn(FF3_qn));  // open: preset, en, reset
  or or_6 (or_6_out, and_9_out, and_10_out, and_11_out);
  and and_12 (and_12_out, FF0_qn, FF1_qn, Q1);
  or or_7 (or_7_out, and_10_out, and_12_out);
  and and_13 (and_13_out, FF3_qn, Q1, FF0_qn);
  or or_8 (or_8_out, and_13_out, and_6_out);
endmodule
