// Logisim project lab 04.circ as structural Verilog: 1 circuit, main circuit main
module main (
  input  W,
  input  X,
  input  Y,
  input  Z,
  output A,
  output B,
  output C,
  output D
);

  wire nor_1_out, nor_2_out, nor_3_out, nor_4_out, nor_5_out, nor_6_out, nor_7_out, nor_8_out, nor_9_out,
       nor_10_out, nor_12_out, nor_13_out, nor_14_out, nor_15_out, nor_16_out, nor_17_out, nor_18_out,
       nor_19_out, nor_20_out;

  nor nor_1 (nor_1_out, X, X);
  nor nor_2 (nor_2_out, W, W);
  nor nor_3 (nor_3_out, Y, Y);
  nor nor_4 (nor_4_out, X, Y);
  nor nor_5 (nor_5_out, X, Z);
  nor nor_6 (nor_6_out, X, X);
  nor nor_7 (nor_7_out, Y, Y);
  nor nor_8 (nor_8_out, Z, Z);
  nor nor_9 (nor_9_out, Z, Z);
  nor nor_10 (nor_10_out, Y, Y);
  nor nor_11 (D, Z, Z);
  nor nor_12 (nor_12_out, Z, Z);
  nor nor_13 (nor_13_out, Y, nor_9_out);
  nor nor_14 (nor_14_out, nor_10_out, Z);
  nor nor_15 (nor_15_out, nor_1_out, nor_2_out);
  nor nor_16 (nor_16_out, nor_2_out, nor_3_out, nor_12_out);
  nor nor_17 (nor_17_out, nor_6_out, nor_7_out, nor_8_out);
  nor nor_18 (nor_18_out, nor_13_out, nor_14_out);
  nor nor_19 (nor_19_out, nor_15_out, nor_16_out);
  nor nor_20 (nor_20_out, nor_4_out, nor_5_out, nor_17_out);
  nor nor_21 (A, nor_19_out, nor_19_out);
  nor nor_22 (C, nor_18_out, nor_18_out);
  nor nor_23 (B, nor_20_out, nor_20_out);
endmodule
