// Logisim project mux final project.circ as structural Verilog: 1 circuit, main circuit main
module main (
  input  in_1,
  input  [2:0] ABC,
  input  D,
  input  in_4,
  input  in_5,
  input  e,
  input  in_7,
  input  e_2,
  input  in_9,
  input  e_3,
  input  in_11,
  input  e_4,
  input  in_13,
  input  in_14
);

  wire D_prime_out, multiplexer_1_out, multiplexer_2_out, multiplexer_3_out, multiplexer_4_out,
       multiplexer_5_out, multiplexer_6_out, multiplexer_7_out, multiplexer_8_out;

  not D_prime (D_prime_out, D);
  Multiplexer #(.select(3), .enable("false")) multiplexer_1 (
    .in0(in_1), .in1(in_1), .in2(D_prime_out), .in3(D_prime_out), .in4(D_prime_out), .in5(D_prime_out),
    .in6(in_1), .in7(in_1), .out(multiplexer_1_out), .sel(ABC));
  Multiplexer #(.select(3), .enable("false")) multiplexer_2 (
    .in0(D), .in1(in_4), .in2(in_4), .in3(D_prime_out), .in4(D), .in5(in_4), .in6(in_4), .in7(in_4),
    .out(multiplexer_2_out), .sel(ABC));
  Multiplexer #(.select(3), .enable("false")) multiplexer_3 (
    .in0(D), .in1(D_prime_out), .in2(D_prime_out), .in3(in_5), .in4(D), .in5(D), .in6(in_5), .in7(in_5),
    .out(multiplexer_3_out), .sel(ABC));
  Multiplexer #(.select(3), .enable("false")) multiplexer_4 (
    .in0(e), .in1(in_7), .in2(D_prime_out), .in3(e), .in4(D_prime_out), .in5(D_prime_out), .in6(in_7),
    .in7(in_7), .out(multiplexer_4_out), .sel(ABC));
  Multiplexer #(.select(3), .enable("false")) multiplexer_5 (
    .in0(D_prime_out), .in1(D_prime_out), .in2(e_2), .in3(e_2), .in4(e_2), .in5(e_2), .in6(in_9), .in7(in_9),
    .out(multiplexer_5_out), .sel(ABC));
  Multiplexer #(.select(3), .enable("false")) multiplexer_6 (
    .in0(e_3), .in1(in_11), .in2(D_prime_out), .in3(e_3), .in4(e_3), .in5(D_prime_out), .in6(in_11),
    .in7(in_11), .out(multiplexer_6_out), .sel(ABC));
  Multiplexer #(.select(3), .enable("false")) multiplexer_7 (
    .in0(D), .in1(e_4), .in2(e_4), .in3(e_4), .in4(D), .in5(e_4), .in6(in_13), .in7(in_13),
    .out(multiplexer_7_out), .sel(ABC));
  Multiplexer #(.select(3), .enable("false")) multiplexer_8 (
    .in0(in_14), .in1(in_14), .in2(in_14), .in3(in_14), .in4(in_14), .in5(in_14), .in6(D_prime_out),
    .in7(in_14), .out(multiplexer_8_out), .sel(ABC));
  _7_Segment_Display u_7_segment_display_1 (
    .g(multiplexer_7_out), .f(multiplexer_6_out), .a(multiplexer_1_out), .b(multiplexer_2_out),
    .e(multiplexer_5_out), .d(multiplexer_4_out), .c(multiplexer_3_out), .dp(multiplexer_8_out));

  // Notes on the sheet:
  //   Name: Jubayed Ahmed Sahel
  //   Id:2221173642
  //   Make All the e switches to 1
endmodule
